# Fritzing sketch Scheme (saved by Fritzing 0.9.3b)

parts:
  Part1 = Arduino Leonardo (Rev3b)
  S1 = H-Bridge with L298N
  M3 = DC Motor
  VCC5 = Battery
  VCC6 = Battery
  VCC7 = Battery
  VCC8 = Battery
  M4 = DC Motor

nets:
  N1: Part1.D1/TX, S1.IN1
  N2: Part1.D2/SDA, S1.IN2
  N3: Part1.D3_PWM/SCL, S1.IN3
  N4: Part1.D4/A6, S1.IN4
  N5: Part1.D5_PWM, S1.ENA, S1.ENA-5V
  N6: Part1.D6_PWM/A7, S1.ENB, S1.ENB-5V
  GND: Part1.GND, S1.GND, VCC8.-
  N7: S1.12V, VCC5.+
  N8: S1.M1-01, M3.pin_1
  N9: S1.M1-02, M3.pin_2
  N10: S1.M2-01, M4.pin_2
  N11: S1.M2-02, M4.pin_1
  N12: VCC5.-, VCC6.+
  N13: VCC6.-, VCC7.+
  N14: VCC7.-, VCC8.+

notes:
  jumper has to be on place!
  wire colors:
  blue, cyan, yellow for one engine
  purple, pink, green for another
  12V battery pack here. Your package may vary

custom parts:
  H-Bridge with L298N: h-bridge
